# Fritzing sketch Untitled Sketch 2 (saved by Fritzing 0.9.3b)
breadboards: 1

parts:
  Part1 = Arduino Uno (Rev3)
  J1 = Basic Servo
  hc-sr1 = hc-sr04
  Part2 = Bluetooth HC-05 Macho  # not connected

nets:
  N1: Part1.A0, hc-sr1.Trig
  N2: Part1.A1, hc-sr1.Echo
  N3: Part1.D6_PWM, J1.pulse
  VCC: Part1.5V, J1.vcc, hc-sr1.VCC
  GND: Part1.GND, J1.gnd, hc-sr1.GND
